# Fritzing sketch PicProgrammer (saved by Fritzing 0.9.3b)
circuit board: 7.14653cm x 4.59721cm
breadboards: 1

parts:
  Часть1 = Arduino Nano (Rev3.0)
  U1 = 4011 4 x 2 Input NAND Gate, multi-part [part_number=4011 package="DIP (Dual Inline) [THT]"]
  Часть2 = 4011_4_x_2_input_NAND_gate_multipart_subpart1 [part_number=4011]
  U1_1 = 4011_4_x_2_input_NAND_gate_multipart_subpart2 [part_number=4011]
  U1_2 = 4011_4_x_2_input_NAND_gate_multipart_subpart3 [part_number=4011]
  U1_3 = 4011_4_x_2_input_NAND_gate_multipart_subpart4 [part_number=4011]
  U1_4 = 4011_4_x_2_input_NAND_gate_multipart_subpart5 [part_number=4011]
  Q2 = NPN-Transistor [package="TO92 [THT]"]
  L1 = Inductor [package="400 mil [THT]"]
  R3 = Resistor [tolerance=±5% resistance=1k package=THT]
  D1 = Rectifier Diode [part_number=1N4001 package="300 mil [THT]"]
  R6 = Resistor [tolerance=±5% resistance=10k package=THT]
  R7 = Resistor [tolerance=±5% resistance=4.7k package=THT]
  Q3 = NPN-Transistor [package="TO92 [THT]"]
  R9 = Resistor [tolerance=±5% resistance=10k package=THT]
  J3 = female pin header, 14 pins [form="♀ (female)"]
  J4 = female pin header, 14 pins [form="♀ (female)"]
  R10 = Resistor [tolerance=±5% resistance=1k package=THT]
  R8 = Resistor [tolerance=±5% resistance=1k package=THT]
  C1 = Electrolytic Capacitor [capacitance=0.22mF package="200 mil [THT, electrolytic]"]
  R1 = Resistor [tolerance=±5% resistance=220 package=THT]
  R2 = Resistor [tolerance=±5% resistance=220 package=THT]
  LED1 = LED - 3mm [color="Red (633nm)" package="3 mm [THT]"]
  LED2 = LED - 3mm [color="Red (633nm)" package="3 mm [THT]"]
  R12 = Resistor [tolerance=±5% resistance=1k package="0603 [SMD]"]
  J5 = female pin header, 3 pins [form="♀ (female)"]
  J6 = female pin header, 3 pins [form="♀ (female)"]
  R11 = Resistor [tolerance=±5% resistance=10k package="0603 [SMD]"]
  Q4 = PNP-Transistor [package="TO92 [THT]"]
  D2 = Rectifier Diode [part_number=1N4001 package="300 mil [THT]"]

nets:
  N1: Часть1.GND, U1.connector6, Часть2.connector6, Q2.E, Q3.E, R9.Pin_0, J3.pin6, J3.pin8, J3.pin9, J3.pin14, J4.pin3, J4.pin4, J4.pin10, C1.-, R1.Pin_1, R2.Pin_1, J5.pin2, R11.Pin_1, D2.anode
  N2: Часть1.D3, U1.connector4, U1.connector5, U1_2.connector4, U1_2.connector5, LED1.anode
  N3: Часть1.D4, J3.pin12, J4.pin2, J4.pin8, J5.pin1
  N4: Часть1.D5, J3.pin13, J4.pin1, J4.pin7, J6.pin1
  N5: Часть1.D9, R3.Pin_0
  N6: Часть1.VIN, U1.connector13, Часть2.connector13, L1.pin_0, R8.Pin_1, R12.Pin_0, Q4.E
  N7: Часть1.A6, U1.connector7, U1.connector8, U1_3.connector7, U1_3.connector8, LED2.anode
  N8: U1.connector0, U1.connector1, U1.connector11, U1.connector12, U1_1.connector0, U1_1.connector1, U1_4.connector11, U1_4.connector12, R12.Pin_1
  N9: U1_2.connector3, R10.Pin_0
  N10: U1_3.connector9, R7.Pin_0
  N11: Q2.B, R3.Pin_1
  N12: Q2.C, L1.pin_1, D1.anode
  N13: D1.cathode, R6.Pin_0, C1.+, D2.cathode
  N14: R6.Pin_1, Q3.C, J3.pin1, J6.pin3
  N15: R7.Pin_1, Q3.B
  N16: R9.Pin_1, J4.pin6, J4.pin9, J4.pin14, J6.pin2, Q4.C
  N17: J3.pin5, J4.pin11, J5.pin3
  N18: J4.pin5, R11.Pin_0
  N19: R10.Pin_1, R8.Pin_0, Q4.B
  N20: R1.Pin_0, LED1.cathode
  N21: R2.Pin_0, LED2.cathode

notes:
  Data
  Clock
